# Fritzing sketch conexiones_ky-006 (saved by Fritzing 1.0.6)

parts:
  M1 = >Wemos D1 R32
  Part1 = KY-006 Passive Buzzer Module [package="Breakout board"]

nets:
  N1: M1.GND, Part1.-
  N2: M1.IO14, Part1.S

custom parts:
  >Wemos D1 R32: Wemos D1 R32 - This board is used with dual-mode Wi-Fi and Bluetooth chips, which is safe, reliable, and scalable to a variety of applications. DC in 5V-12V, 1 analog input(3.2V max input), a Micro USB connection, Compatible with D1 R32=WiFi+bluetooth+UNO
  KY-006 Passive Buzzer Module: Passive Piezoelectric Buzzer Module Keyes KY-006, it can produce a range of sound tones depending on the input frequency.
