# Fritzing sketch conexiones_motor_a_pasos (saved by Fritzing 1.0.6)

parts:
  M1 = >Wemos D1 R32
  Driver1 = 28BYJ-48 Driver Module [part_number=ULN2003 package=THT]
  SM1 = 28BYJ-48 Stepper Motor [part_number=28BYJ-48]  # not connected

nets:
  N1: M1.5V, Driver1.Vmotor
  GND: M1.GND, Driver1.GND
  N2: M1.IO26, Driver1.IN4
  N3: M1.IO25, Driver1.IN3
  N4: M1.IO17, Driver1.IN2
  N5: M1.IO16, Driver1.IN1

custom parts:
  >Wemos D1 R32: Wemos D1 R32 - This board is used with dual-mode Wi-Fi and Bluetooth chips, which is safe, reliable, and scalable to a variety of applications. DC in 5V-12V, 1 analog input(3.2V max input), a Micro USB connection, Compatible with D1 R32=WiFi+bluetooth+UNO
  28BYJ-48 Driver Module: High-power ULN2003 Stepper Motor Driver Board Test Module For Arduino AVR SMD
  28BYJ-48 Stepper Motor: Unipolar Stepper Motor 28BYJ-48 Top coil - pink & orange Bottom coil - blue & yellow Common rail - red Connector pins: blue - pink - yellow - orange - red
