# Fritzing sketch conexiones_hc-05 (saved by Fritzing 1.0.6)

parts:
  M1 = >Wemos D1 R32
  BT1 = Bluetooth HC-06u [package=THT]

nets:
  5V: M1.5V, BT1.VCC
  GND: M1.GND, BT1.GND
  N1: M1.IO17, BT1.RXD
  N2: M1.IO16, BT1.TXD

custom parts:
  >Wemos D1 R32: Wemos D1 R32 - This board is used with dual-mode Wi-Fi and Bluetooth chips, which is safe, reliable, and scalable to a variety of applications. DC in 5V-12V, 1 analog input(3.2V max input), a Micro USB connection, Compatible with D1 R32=WiFi+bluetooth+UNO
  Bluetooth HC-06u: Bluetooth HC-06 - face up, pins down 16.5mm x 37.5mm PCB
