# Fritzing sketch conexiones_display (saved by Fritzing 1.0.6)
breadboards: 1

parts:
  M1 = >Wemos D1 R32
  DI1 = 7-Segment LED Display [package=THT]

nets:
  N1: M1.GND, DI1.commAnode#2
  N2: M1.IO14, DI1.cathodeE
  N3: M1.IO12, DI1.cathodeD
  N4: M1.IO13, DI1.cathodeC
  N5: M1.IO5, DI1.cathodeB
  N6: M1.IO23, DI1.cathodeA
  N7: M1.IO19, DI1.cathodeF
  N8: M1.IO18, DI1.cathodeG

custom parts:
  >Wemos D1 R32: Wemos D1 R32 - This board is used with dual-mode Wi-Fi and Bluetooth chips, which is safe, reliable, and scalable to a variety of applications. DC in 5V-12V, 1 analog input(3.2V max input), a Micro USB connection, Compatible with D1 R32=WiFi+bluetooth+UNO
