# Fritzing sketch conexiones_matrix (saved by Fritzing 1.0.6)

parts:
  M1 = >Wemos D1 R32
  Componente1 = LED Matrix - Serial Interface - Red/Green/Blue

nets:
  3V3: M1.3V3, Componente1.VCC
  N1: M1.IO13, Componente1.MISO
  N2: M1.IO5, Componente1.CS
  N3: M1.IO18, Componente1.SCK
  GND: M1.GND, Componente1.GND

custom parts:
  >Wemos D1 R32: Wemos D1 R32 - This board is used with dual-mode Wi-Fi and Bluetooth chips, which is safe, reliable, and scalable to a variety of applications. DC in 5V-12V, 1 analog input(3.2V max input), a Micro USB connection, Compatible with D1 R32=WiFi+bluetooth+UNO
