# Fritzing sketch conexiones_neopixel8x8 (saved by Fritzing 1.0.6)

parts:
  M1 = >Wemos D1 R32
  U1 = WS2812 RGB LED matrix 8x8

nets:
  5V: M1.5V, U1.VCC
  GND: M1.GND, U1.GND
  N1: M1.IO14, U1.DIN

custom parts:
  >Wemos D1 R32: Wemos D1 R32 - This board is used with dual-mode Wi-Fi and Bluetooth chips, which is safe, reliable, and scalable to a variety of applications. DC in 5V-12V, 1 analog input(3.2V max input), a Micro USB connection, Compatible with D1 R32=WiFi+bluetooth+UNO
  WS2812 RGB LED matrix 8x8: WS2812 matrix 8x8
