# Fritzing sketch conexiones_oled (saved by Fritzing 1.0.6)

parts:
  M1 = >Wemos D1 R32
  OLED1 = OLED 128x64 I2C Monochrome Display

nets:
  3V3: M1.3V3, OLED1.VDD
  GND: M1.GND, OLED1.GND
  N1: M1.SDA, OLED1.SDA
  N2: M1.SCL, OLED1.SCK

custom parts:
  >Wemos D1 R32: Wemos D1 R32 - This board is used with dual-mode Wi-Fi and Bluetooth chips, which is safe, reliable, and scalable to a variety of applications. DC in 5V-12V, 1 analog input(3.2V max input), a Micro USB connection, Compatible with D1 R32=WiFi+bluetooth+UNO
