# Fritzing sketch conexiones_tft_240x240 (saved by Fritzing 1.0.6)

parts:
  A1 = lcd color display 1.3in 240x240 7pin interface [package=THT]
  M1 = >Wemos D1 R32

nets:
  GND: A1.GND, M1.GND
  VCC: A1.VCC, M1.3V3
  N1: A1.SCL, M1.IO18
  N2: A1.SDA, M1.IO19
  N3: A1.RES, M1.SCL
  N4: A1.DC, M1.SDA

custom parts:
  lcd color display 1.3in 240x240 7pin interface: 1.3 Inch Color 240 x 240 IPS TFT LCD Display Screen Module Board 7 Pin 4 Wire ST7789VW Drive IC SPI interface.
  >Wemos D1 R32: Wemos D1 R32 - This board is used with dual-mode Wi-Fi and Bluetooth chips, which is safe, reliable, and scalable to a variety of applications. DC in 5V-12V, 1 analog input(3.2V max input), a Micro USB connection, Compatible with D1 R32=WiFi+bluetooth+UNO
