# Fritzing sketch encoder (saved by Fritzing 1.0.6)

parts:
  M1 = >Wemos D1 R32
  RE1 = KY-040 Rotary encoder [package=THT]

nets:
  3V3: M1.3V3, RE1.Vcc
  N1: M1.IO19, RE1.CLK
  N2: M1.IO18, RE1.DT
  GND: M1.GND, RE1.GND

custom parts:
  >Wemos D1 R32: Wemos D1 R32 - This board is used with dual-mode Wi-Fi and Bluetooth chips, which is safe, reliable, and scalable to a variety of applications. DC in 5V-12V, 1 analog input(3.2V max input), a Micro USB connection, Compatible with D1 R32=WiFi+bluetooth+UNO
  KY-040 Rotary encoder: KY-040 Rotary Encoder with switch on breakout borad from AZ Delivery
