# Fritzing sketch conexiones_bmp280 (saved by Fritzing 1.0.6)

parts:
  M1 = >Wemos D1 R32
  Componente1 = Adafruit_BMP280

nets:
  3V3: M1.3V3, Componente1.3.3V
  GND: M1.GND, Componente1.GND
  N1: M1.SDA, Componente1.SDO/ADR
  N2: M1.SCL, Componente1.SCK/SCL

custom parts:
  >Wemos D1 R32: Wemos D1 R32 - This board is used with dual-mode Wi-Fi and Bluetooth chips, which is safe, reliable, and scalable to a variety of applications. DC in 5V-12V, 1 analog input(3.2V max input), a Micro USB connection, Compatible with D1 R32=WiFi+bluetooth+UNO
  Adafruit_BMP280: Bosch has stepped up their game with their new BMP280 sensor, an environmental sensor with temperature, barometric pressure that is the next generation upgrade to the BMP085/BMP180/BMP183. This sensor is great for all sorts of weather sensing and can even be used in both I2C and SPI! This precision sensor from Bosch is the best low-cost, precision sensing solution for measuring barometric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
