# Fritzing sketch conexiones_ds3231 (saved by Fritzing 1.0.6)

parts:
  M1 = >Wemos D1 R32
  ZS-042_RTC1 = ZS-042 RTC Module

nets:
  3V3: M1.3V3, ZS-042_RTC1.VCC
  GND: M1.GND, ZS-042_RTC1.GND
  N1: M1.SDA, ZS-042_RTC1.SDA
  N2: M1.SCL, ZS-042_RTC1.SCL

custom parts:
  >Wemos D1 R32: Wemos D1 R32 - This board is used with dual-mode Wi-Fi and Bluetooth chips, which is safe, reliable, and scalable to a variety of applications. DC in 5V-12V, 1 analog input(3.2V max input), a Micro USB connection, Compatible with D1 R32=WiFi+bluetooth+UNO
