# Fritzing sketch conexiones_hmc5883 (saved by Fritzing 1.0.6)

parts:
  M1 = >Wemos D1 R32
  BREAKOUT1 = HMC5883L Compass Breakout

nets:
  N1: M1.3V3, BREAKOUT1.3vo
  GND: M1.GND, BREAKOUT1.GND
  N2: M1.SDA, BREAKOUT1.SDA
  N3: M1.SCL, BREAKOUT1.SCL

custom parts:
  >Wemos D1 R32: Wemos D1 R32 - This board is used with dual-mode Wi-Fi and Bluetooth chips, which is safe, reliable, and scalable to a variety of applications. DC in 5V-12V, 1 analog input(3.2V max input), a Micro USB connection, Compatible with D1 R32=WiFi+bluetooth+UNO
