# Fritzing sketch conexiones_mpu5060 (saved by Fritzing 1.0.6)

parts:
  M1 = >Wemos D1 R32
  GY1 = MPU-6050 Board GY-521 [form="♀ (female)" package=THT]

nets:
  N1: M1.3V3, GY1.pin1
  N2: M1.GND, GY1.pin2
  N3: M1.SDA, GY1.pin4
  N4: M1.SCL, GY1.pin3

custom parts:
  >Wemos D1 R32: Wemos D1 R32 - This board is used with dual-mode Wi-Fi and Bluetooth chips, which is safe, reliable, and scalable to a variety of applications. DC in 5V-12V, 1 analog input(3.2V max input), a Micro USB connection, Compatible with D1 R32=WiFi+bluetooth+UNO
  MPU-6050 Board GY-521: Acelerometro y Giroscopio MPU-6050 Board GY-521
