# Fritzing sketch conexion_tcs34725 (saved by Fritzing 1.0.6)

parts:
  M1 = >Wemos D1 R32
  SENSOR1 = TCS34725 RGB Color Sensor

nets:
  3V3: M1.3V3, SENSOR1.3V3
  GND: M1.GND, SENSOR1.GND
  N1: M1.SDA, SENSOR1.SDA
  N2: M1.SCL, SENSOR1.SCL

custom parts:
  >Wemos D1 R32: Wemos D1 R32 - This board is used with dual-mode Wi-Fi and Bluetooth chips, which is safe, reliable, and scalable to a variety of applications. DC in 5V-12V, 1 analog input(3.2V max input), a Micro USB connection, Compatible with D1 R32=WiFi+bluetooth+UNO
  TCS34725 RGB Color Sensor: TCS34725 RGB Color Sensor with LED
