# Fritzing sketch tcs34725 (saved by Fritzing 1.0.6)

parts:
  M1 = >Wemos D1 R32
  Componente1 = Adafruit TCS34725 RGB Color Sensor [part_number="Adafruit #1334"]

nets:
  3V3: M1.3V3, Componente1.+3V3
  GND: M1.GND, Componente1.GND
  N1: M1.SDA, Componente1.SDA
  N2: M1.SCL, Componente1.SCL

custom parts:
  >Wemos D1 R32: Wemos D1 R32 - This board is used with dual-mode Wi-Fi and Bluetooth chips, which is safe, reliable, and scalable to a variety of applications. DC in 5V-12V, 1 analog input(3.2V max input), a Micro USB connection, Compatible with D1 R32=WiFi+bluetooth+UNO
  Adafruit TCS34725 RGB Color Sensor: Your electronics can now see in dazzling color with this lovely color light sensor. We found the best color sensor on the market, the TCS34725, which has RGB and Clear light sensing elements. An IR blocking filter, integrated on-chip and localized to the color sensing photodiodes, minimizes the IR spectral component of the incoming light and allows color measurements to be made accurately. The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
