# Fritzing sketch conexiones_rfid (saved by Fritzing 1.0.6)

parts:
  M1 = >Wemos D1 R32
  Componente1 = RFID-RC522-v2

nets:
  3V3: M1.3V3, Componente1.3.3V
  N1: M1.IO23, Componente1.MOSI
  N2: M1.IO19, Componente1.MISO
  N3: M1.IO18, Componente1.SCK
  GND: M1.GND, Componente1.GND
  N4: M1.SDA, Componente1.SDA
  N5: M1.SCL, Componente1.RST

custom parts:
  >Wemos D1 R32: Wemos D1 R32 - This board is used with dual-mode Wi-Fi and Bluetooth chips, which is safe, reliable, and scalable to a variety of applications. DC in 5V-12V, 1 analog input(3.2V max input), a Micro USB connection, Compatible with D1 R32=WiFi+bluetooth+UNO
  RFID-RC522-v2: A simple China made RFID-RC522 Reader; do check the pin labels, as this is a MFRC522 based clone.
