# Fritzing sketch conexiones_sd (saved by Fritzing 1.0.6)

parts:
  M1 = >Wemos D1 R32
  microSD1 = MicroSD Card Module

nets:
  5V: M1.5V, microSD1.VCC
  GND: M1.GND, microSD1.GND
  N1: M1.IO5, microSD1.CS
  N2: M1.IO23, microSD1.MOSI
  N3: M1.IO19, microSD1.MISO
  N4: M1.IO18, microSD1.SCK

custom parts:
  >Wemos D1 R32: Wemos D1 R32 - This board is used with dual-mode Wi-Fi and Bluetooth chips, which is safe, reliable, and scalable to a variety of applications. DC in 5V-12V, 1 analog input(3.2V max input), a Micro USB connection, Compatible with D1 R32=WiFi+bluetooth+UNO
  MicroSD Card Module: A common microSD card module.
