# Fritzing sketch conexiones_cp2102 (saved by Fritzing 1.0.6)

parts:
  M1 = >Wemos D1 R32
  FTDI_USB_UART1 = CP2102 USB UART [part_number="USB UART"]

nets:
  3V3: M1.3V3, FTDI_USB_UART1.3V3
  N1: M1.IO17, FTDI_USB_UART1.RXI
  N2: M1.IO16, FTDI_USB_UART1.TXO
  GND: M1.GND, FTDI_USB_UART1.GND

custom parts:
  >Wemos D1 R32: Wemos D1 R32 - This board is used with dual-mode Wi-Fi and Bluetooth chips, which is safe, reliable, and scalable to a variety of applications. DC in 5V-12V, 1 analog input(3.2V max input), a Micro USB connection, Compatible with D1 R32=WiFi+bluetooth+UNO
  CP2102 USB UART: CP2102 USB UART FTDI
