# Fritzing sketch conexiones_hmc5883l (saved by Fritzing 1.0.6)

parts:
  BREAKOUT1 = HMC5883L Compass Breakout
  M1 = >Wemos D1 R32

nets:
  N1: BREAKOUT1.SCL, M1.SCL
  N2: BREAKOUT1.SDA, M1.SDA
  GND: BREAKOUT1.GND, M1.GND
  VIN: BREAKOUT1.VIN, M1.3V3

custom parts:
  >Wemos D1 R32: Wemos D1 R32 - This board is used with dual-mode Wi-Fi and Bluetooth chips, which is safe, reliable, and scalable to a variety of applications. DC in 5V-12V, 1 analog input(3.2V max input), a Micro USB connection, Compatible with D1 R32=WiFi+bluetooth+UNO
