# Fritzing sketch conexiones_mp3_player (saved by Fritzing 1.0.6)

parts:
  M1 = >Wemos D1 R32
  DFPlayer_Mini1 = DFPlayer MINI [package="DIP (Dual Inline) [THT]"]
  J1 = Piezo Speaker  # not connected

nets:
  5V: M1.5V, DFPlayer_Mini1.VCC
  N1: M1.IO17, DFPlayer_Mini1.RX
  N2: M1.IO16, DFPlayer_Mini1.TX
  GND: M1.GND, DFPlayer_Mini1.GND

custom parts:
  >Wemos D1 R32: Wemos D1 R32 - This board is used with dual-mode Wi-Fi and Bluetooth chips, which is safe, reliable, and scalable to a variety of applications. DC in 5V-12V, 1 analog input(3.2V max input), a Micro USB connection, Compatible with D1 R32=WiFi+bluetooth+UNO
  DFPlayer MINI: MP3 module by DFRobot.com for playing Music from an SD-Card. Supports WAV and MP3 files.
