# Fritzing sketch conexiones_teclado4x3 (saved by Fritzing 1.0.6)

parts:
  KEYPAD1 = Membrane Matrix Keypad
  M1 = >Wemos D1 R32

nets:
  N1: KEYPAD1.1, M1.IO26
  N2: KEYPAD1.2, M1.IO25
  N3: KEYPAD1.3, M1.IO17
  N4: KEYPAD1.4, M1.IO16
  N5: KEYPAD1.5, M1.IO27
  N6: KEYPAD1.6, M1.IO14
  N7: KEYPAD1.7, M1.IO12

custom parts:
  Membrane Matrix Keypad: Membrane Matrix 3x4 Keypad
  >Wemos D1 R32: Wemos D1 R32 - This board is used with dual-mode Wi-Fi and Bluetooth chips, which is safe, reliable, and scalable to a variety of applications. DC in 5V-12V, 1 analog input(3.2V max input), a Micro USB connection, Compatible with D1 R32=WiFi+bluetooth+UNO
