# Fritzing sketch conexiones_teclado4x4 (saved by Fritzing 1.0.6)

parts:
  M1 = >Wemos D1 R32
  Keypad4x1 = Keypad Membran 4x4

nets:
  N1: M1.IO26, Keypad4x1.Pin1
  N2: M1.IO25, Keypad4x1.Pin2
  N3: M1.IO17, Keypad4x1.Pin3
  N4: M1.IO16, Keypad4x1.Pin4
  N5: M1.IO27, Keypad4x1.Pin5
  N6: M1.IO14, Keypad4x1.Pin6
  N7: M1.IO12, Keypad4x1.Pin7
  N8: M1.IO13, Keypad4x1.Pin8

custom parts:
  >Wemos D1 R32: Wemos D1 R32 - This board is used with dual-mode Wi-Fi and Bluetooth chips, which is safe, reliable, and scalable to a variety of applications. DC in 5V-12V, 1 analog input(3.2V max input), a Micro USB connection, Compatible with D1 R32=WiFi+bluetooth+UNO
  Keypad Membran 4x4: Membrane Keypad 4x4 Matrix
