# Fritzing sketch conexiones_teclado4x4_i2c (saved by Fritzing 1.0.6)

parts:
  M1 = pcf8574 io expansion board [package=THT]
  Keypad4x1 = Keypad Membran 4x4
  M2 = >Wemos D1 R32

nets:
  VCC: M1.VCC, M2.3V3
  GND: M1.GND, M2.GND
  N1: M1.SDA, M2.SDA
  N2: M1.SCL, M2.SCL
  N3: M1.O0, Keypad4x1.Pin1
  N4: M1.O1, Keypad4x1.Pin2
  N5: M1.O2, Keypad4x1.Pin3
  N6: M1.O3, Keypad4x1.Pin4
  N7: M1.O4, Keypad4x1.Pin5
  N8: M1.O5, Keypad4x1.Pin6
  N9: M1.O6, Keypad4x1.Pin7
  N10: M1.O7, Keypad4x1.Pin8

custom parts:
  pcf8574 io expansion board: pcf8574 io expansion board.
  Keypad Membran 4x4: Membrane Keypad 4x4 Matrix
  >Wemos D1 R32: Wemos D1 R32 - This board is used with dual-mode Wi-Fi and Bluetooth chips, which is safe, reliable, and scalable to a variety of applications. DC in 5V-12V, 1 analog input(3.2V max input), a Micro USB connection, Compatible with D1 R32=WiFi+bluetooth+UNO
