# Fritzing sketch conexiones_adkey (saved by Fritzing 1.0.6)

parts:
  M1 = >Wemos D1 R32
  J1 = Generic female header - 2 pins [form="♀ (female)" package=THT]

nets:
  3V3: M1.3V3, J1.VCC
  GND: M1.GND, J1.GND
  N1: M1.IO35, J1.OUT

custom parts:
  >Wemos D1 R32: Wemos D1 R32 - This board is used with dual-mode Wi-Fi and Bluetooth chips, which is safe, reliable, and scalable to a variety of applications. DC in 5V-12V, 1 analog input(3.2V max input), a Micro USB connection, Compatible with D1 R32=WiFi+bluetooth+UNO
  Generic female header - 2 pins: Generic female header
