# Fritzing sketch conexiones_ky-022 (saved by Fritzing 1.0.6)

parts:
  M1 = >Wemos D1 R32
  Part1 = KY-022 Infrared Receiver Module [package="Breakout board"]

nets:
  3V3: M1.3V3, Part1.Vin
  N1: M1.IO12, Part1.S
  N2: M1.GND, Part1.-

custom parts:
  >Wemos D1 R32: Wemos D1 R32 - This board is used with dual-mode Wi-Fi and Bluetooth chips, which is safe, reliable, and scalable to a variety of applications. DC in 5V-12V, 1 analog input(3.2V max input), a Micro USB connection, Compatible with D1 R32=WiFi+bluetooth+UNO
  KY-022 Infrared Receiver Module: Arduino IR receiver module KY-022, reacts to 38kHz infrared light.
