# Fritzing sketch conexiones_joystick (saved by Fritzing 1.0.6)

parts:
  M1 = >Wemos D1 R32
  Componente1 = Black Joystick KY-023

nets:
  3V3: M1.3V3, Componente1.+5V
  GND: M1.GND, Componente1.GND
  N1: M1.IO4, Componente1.SW
  N2: M1.IO35, Componente1.VRy
  N3: M1.IO34, Componente1.VRx

custom parts:
  >Wemos D1 R32: Wemos D1 R32 - This board is used with dual-mode Wi-Fi and Bluetooth chips, which is safe, reliable, and scalable to a variety of applications. DC in 5V-12V, 1 analog input(3.2V max input), a Micro USB connection, Compatible with D1 R32=WiFi+bluetooth+UNO
  Black Joystick KY-023: Description: The joystick is a combination of 2 analoog potentiometer and a digital switch. Arduino GND --> Module pin - Arduino +5V --> Module pin +5V Arduino Analoog 0 --> Module VRx Arduino Analoog 1 --> Module VRy Arduino Digital --> Module SW Dimensions: 1" x 1.25"
