# Fritzing sketch conexiones_mq2 (saved by Fritzing 1.0.6)

parts:
  A1 = MQ-2 breakout
  M1 = >Wemos D1 R32

nets:
  VCC: A1.VCC, M1.3V3
  GND: A1.GND, M1.GND
  N1: A1.DO, M1.IO18
  N2: A1.AO, M1.IO13

custom parts:
  MQ-2 breakout: MQ-2 gas sensor
  >Wemos D1 R32: Wemos D1 R32 - This board is used with dual-mode Wi-Fi and Bluetooth chips, which is safe, reliable, and scalable to a variety of applications. DC in 5V-12V, 1 analog input(3.2V max input), a Micro USB connection, Compatible with D1 R32=WiFi+bluetooth+UNO
