# Fritzing sketch conexiones_ky-001 (saved by Fritzing 1.0.6)

parts:
  M1 = >Wemos D1 R32
  Part1 = KY-001 Temperature Sensor Module [package="Breakout board"]

nets:
  3V3: M1.3V3, Part1.Vin
  N1: M1.IO12, Part1.S
  N2: M1.GND, Part1.-

custom parts:
  >Wemos D1 R32: Wemos D1 R32 - This board is used with dual-mode Wi-Fi and Bluetooth chips, which is safe, reliable, and scalable to a variety of applications. DC in 5V-12V, 1 analog input(3.2V max input), a Micro USB connection, Compatible with D1 R32=WiFi+bluetooth+UNO
  KY-001 Temperature Sensor Module: Arduino Temperature Sensor Module Keyes KY-001, Allows ambient temperature measurement using digital serial bus (DS18B20)
