# Fritzing sketch conexiones_ky-015 (saved by Fritzing 1.0.6)

parts:
  M1 = >Wemos D1 R32
  DHT11_1 = DHT11 module

nets:
  3V3: M1.3V3, DHT11_1.VCC
  GND: M1.GND, DHT11_1.GND
  N1: M1.IO13, DHT11_1.DATA

custom parts:
  >Wemos D1 R32: Wemos D1 R32 - This board is used with dual-mode Wi-Fi and Bluetooth chips, which is safe, reliable, and scalable to a variety of applications. DC in 5V-12V, 1 analog input(3.2V max input), a Micro USB connection, Compatible with D1 R32=WiFi+bluetooth+UNO
  DHT11 module: DHT11 black pcb module
