# Fritzing sketch conexciones_ultrasonico (saved by Fritzing 1.0.6)

parts:
  M1 = >Wemos D1 R32
  HC-SR04_Sensor_1 = HC-SR04 Ultrasonic Distance Sensor

nets:
  3V3: M1.3V3, HC-SR04_Sensor_1.VCC
  GND: M1.GND, HC-SR04_Sensor_1.GND
  N1: M1.IO12, HC-SR04_Sensor_1.TRIG
  N2: M1.IO13, HC-SR04_Sensor_1.ECHO

custom parts:
  >Wemos D1 R32: Wemos D1 R32 - This board is used with dual-mode Wi-Fi and Bluetooth chips, which is safe, reliable, and scalable to a variety of applications. DC in 5V-12V, 1 analog input(3.2V max input), a Micro USB connection, Compatible with D1 R32=WiFi+bluetooth+UNO
  HC-SR04 Ultrasonic Distance Sensor: The HC-SR04 is an ultrasonic distance sensor. It is capable of providing measurement for ranges of 2cm to 400cm. The module operates at 5V.
